# Fritzing sketch controlRemoto (saved by Fritzing 0.9.3b)
breadboards: 1

parts:
  Arduino_Uno = Arduino Uno (Rev3) - ICSP
  LED1 = LED - 5mm [color="Red (633nm)" package="5 mm [THT]"]
  Sensor_Flame = LED - 5mm [color="Red (633nm)" package="5 mm [THT]"]
  Resistencia_1k = Resistor [tolerance=±5% resistance=220 package=THT]

nets:
  N1: Arduino_Uno.A0, Sensor_Flame.cathode, Resistencia_1k.Pin_0
  N2: Arduino_Uno.D13/SCK, LED1.anode
  N3: Arduino_Uno.GND, LED1.cathode, Resistencia_1k.Pin_1
  N4: Arduino_Uno.5V, Sensor_Flame.anode

notes:
  Sensor Flama kuman
  Se conecta al pin A0.
  para hacer pruebas puedes usar un mechero.
  Con el código al hacer la llama enciendes el led rojo.
  Puedes usar el pin 13, o añadir uno como un led rojo.
  No necesita resistencia en este pin.
